# Fritzing sketch schema (saved by Fritzing 1.0.1rc)

parts:
  J1 = Basic Servo
  A1 = tf-luna lidar
  A2 = VL53lox
  A3 = VL53lox
  J2 = female pin header, 15 pins [form="♀ (female)"]
  J3 = female pin header, 15 pins [form="♀ (female)"]
  J5 = Dagu DGServo 9g header (male) [package=THT]
  Composant1 = Lilypad Power Supply
  S1 = Pushbutton [package=THT]
  J6 = female pin header, 6 pins [form="♀ (female)"]

nets:
  GND: J1.gnd, A1.Pin_6, A2.Pin_2, A3.Pin_2, J2.pin14, J5.pulse, Composant1.GND, S1.leg1, J6.pin4, J6.pin5
  VCC: J1.vcc, A2.Pin_1, A3.Pin_1, J2.pin15, J5.Vcc, Composant1.+, J6.pin1
  N1: J1.pulse, J3.pin10
  N2: A1.Pin_1, A2.Pin_3, A3.Pin_3, J3.pin2, J6.pin2
  N3: A1.Pin_3, A1.Pin_4, A2.Pin_4, A3.Pin_4, J3.pin5, J6.pin3
  N4: A3.Pin_6, J3.pin7
  N5: J3.pin1, S1.leg0
  N6: J3.pin13, J5.gnd

notes:
  5V
  vitesse moteur
  direction
  D15
  D16
  SCL
  SDA
  D23
  stop vitesse moteur
  Ft mini Luna

custom parts:
  tf-luna lidar: TF-Luna is using Time of Flight (TOF) principle to measure distance, and it periodically emits near infrared modulated wave.
  VL53lox: VL53L0X Time-of-Flight (ToF) Laser Ranging Sensor Breakout.
